// Logisim project A2_group6_final.circ as structural Verilog: 1 circuit, main circuit main
module main (
  input  cs2,
  input  cs1,
  input  cs0,
  input  b4,
  input  b3,
  input  b2,
  input  b1,
  input  a4,
  input  a3,
  input  a2,
  input  a1,
  output v,
  output z,
  output c,
  output s,
  output Cout,
  output s4,
  output s3,
  output s2,
  output s1
);

  wire n7404_1_p9, n7408_1_p3, n7408_1_p6, n7408_1_p11, n7408_1_p14, n7408_2_p3, n7408_2_p6, n7408_2_p11,
       n7408_2_p14, n7408_3_p3, n7408_3_p4, n7408_4_p3, n7408_4_p4, n7408_4_p5, n7408_4_p6, n7408_4_p10,
       n7408_4_p11, n7408_4_p14, n7432_1_p3, n7432_1_p6, n7432_1_p11, n7432_1_p14, n7432_2_p3, n7432_2_p6,
       n7432_2_p11, n7432_2_p14, n7432_3_p3, n7432_3_p6, n7486_1_p3, n7486_1_p6, n7486_1_p11, n7486_1_p14,
       n74153_1_p6, n74153_1_p14, n74153_2_p6, n74153_2_p14, n74238_1_p7, n74238_1_p8, n74238_1_p9,
       n74238_1_p10, n74238_1_p11, n74238_1_p12, n74238_1_p13;

  // _74238 74238_1: pin names not known; wires that end beside it: cs0, cs1, cs2, 1'b0, 1'b0, 1'b1, n74238_1_p7, n74238_1_p8, n74238_1_p9, n74238_1_p10, n74238_1_p11, n74238_1_p12, n74238_1_p13
  // _7408 7408_1: pin names not known; wires that end beside it: a4, b4, n7408_1_p3, a3, b3, n7408_1_p6, 1'b0, 1'b1, a2, b2, n7408_1_p11, a1, b1, n7408_1_p14
  // _7486 7486_1: pin names not known; wires that end beside it: a4, b4, n7486_1_p3, a3, b3, n7486_1_p6, 1'b0, 1'b1, a2, b2, n7486_1_p11, a1, b1, n7486_1_p14
  // _7432 7432_1: pin names not known; wires that end beside it: n74238_1_p8, n74238_1_p9, n7432_1_p3, n74238_1_p13, n74238_1_p7, n7432_1_p6, 1'b0, 1'b1, n74238_1_p10, n74238_1_p11, n7432_1_p11, n74238_1_p12, n7432_1_p11, n7432_1_p14
  // _74153 74153_1: pin names not known; wires that end beside it: 1'b0, n74238_1_p12, n7486_1_p3, n7408_1_p3, a4, n74153_1_p6, 1'b0, 1'b1, 1'b0, n7432_1_p11, n7486_1_p6, n7408_1_p6, a3, n74153_1_p14
  // _74153 74153_2: pin names not known; wires that end beside it: 1'b0, n74238_1_p12, n7486_1_p11, n7408_1_p11, a2, n74153_2_p6, 1'b0, 1'b1, 1'b0, n7432_1_p11, n7486_1_p14, n7408_1_p14, a1, n74153_2_p14
  // _7408 7408_2: pin names not known; wires that end beside it: n7432_1_p3, b4, n7408_2_p3, n7432_1_p3, b3, n7408_2_p6, 1'b0, 1'b1, n7432_1_p3, b2, n7408_2_p11, n7432_1_p3, b1, n7408_2_p14
  // _7432 7432_2: pin names not known; wires that end beside it: n7432_1_p6, n7408_2_p3, n7432_2_p3, n7432_1_p6, n7408_2_p6, n7432_2_p6, 1'b0, 1'b1, n7432_1_p6, n7408_2_p11, n7432_2_p11, n7432_1_p6, n7408_2_p14, n7432_2_p14
  // _7483 7483_1: pin names not known; wires that end beside it: n74153_1_p6, s3, n74153_1_p14, n7432_2_p6, 1'b1, s2, n7432_2_p11, n74153_2_p6, n7432_2_p3, s, c, n74238_1_p9, 1'b0, n7432_2_p14, n74153_2_p14, s1
  // _7408 7408_3: pin names not known; wires that end beside it: 1'b0, 1'b1, n7408_3_p3, n7408_3_p4, v
  // _7408 7408_4: pin names not known; wires that end beside it: n74153_1_p6, n7432_2_p3, n7408_4_p3, n7408_4_p4, n7408_4_p5, n7408_4_p6, 1'b0, 1'b1, n7408_4_p3, n7408_4_p10, n7408_4_p11, n7408_4_p6, s, n7408_4_p14
  // _7404 7404_1: pin names not known; wires that end beside it: n7432_2_p3, n7408_4_p4, n74153_1_p6, n7408_4_p5, s, n7408_4_p10, 1'b0, 1'b1, n7404_1_p9, z, n7432_1_p14, n7408_3_p3
  // _7432 7432_3: pin names not known; wires that end beside it: s, s3, n7432_3_p3, n7432_3_p3, s2, n7432_3_p6, 1'b0, 1'b1, n7408_4_p11, n7408_4_p14, n7408_3_p4, s1, n7432_3_p6, n7404_1_p9

  assign Cout = c;
  assign s4 = s;
endmodule
