// Logisim project A2_Group6.circ as structural Verilog: 23 circuits, main circuit 11.Block_Diagram_2
module _1_Main_Circuit (
  input  [31:0] Number_A,
  input  [31:0] Number_B,
  output Output_sign,
  output [31:0] Output_Significand,
  output equal_expononet,
  output Overflow,
  output underflow,
  output [11:0] Output_exponent,
  output [31:0] Output_result
);

  wire comparator_1_eq, comparator_2_eq, n7408_1_p3;
  wire [11:0] Alignment_and_shifting_larger_exp, Normalization_normalized_expo;
  wire [21:0] Alignment_and_shifting_fraction_bit_a_2, Alignment_and_shifting_fraction_shifted;
  wire [31:0] _32_bit_Adder_output_significand, Normalization_normalized_frac, Rounding_output_significand;

  Comparator #(.width(32), .mode("unsigned")) comparator_1 (
    .a(Number_B), .b({32{1'b0}}), .eq(comparator_1_eq));  // open: gt, lt
  Comparator #(.width(32), .mode("unsigned")) comparator_2 (
    .a(Number_A), .b({32{1'b0}}), .eq(comparator_2_eq));  // open: gt, lt
  _2_Alignment_Input Alignment_and_shifting (
    .Fraction_Bit_A(Number_A[18:0]), .Fraction_Bit_B(Number_B[18:0]), .Exp_Bit_A(Number_A[30:19]),
    .Exp_Bit_B(Number_B[30:19]), .Sign_Bit_A(Number_A[31]), .Sign_Bit_B(Number_B[31]),
    .Equal_exponent(equal_expononet), .Fraction_Bit_A_2(Alignment_and_shifting_fraction_bit_a_2),
    .Fraction_Shifted(Alignment_and_shifting_fraction_shifted),
    .Larger_Exp(Alignment_and_shifting_larger_exp), .Output_sign(Output_sign));  // open: out_10, Exp_difference
  // _7408 7408_1: pin names not known; wires that end beside it: comparator_1_eq, comparator_2_eq, n7408_1_p3
  _5_Adder_Circuit _32_bit_Adder (
    .sign_bit_A(Number_A[31]), .sign_bit_B(Number_B[31]),
    .Significand_A(Alignment_and_shifting_fraction_bit_a_2),
    .Significand_B(Alignment_and_shifting_fraction_shifted),
    .Output_significand(_32_bit_Adder_output_significand));  // open: out_6, out_7
  _6_Normalize_Output Normalization (
    .Input_Significand(_32_bit_Adder_output_significand), .Input_Exponent(Alignment_and_shifting_larger_exp),
    .Normalized_frac(Normalization_normalized_frac), .Normalized_expo(Normalization_normalized_expo));  // open: overflow, undeflow, _29__Position, Position, present
  _7_Rounding_Bits Rounding (
    .Output_Significand(Rounding_output_significand), .Input_significand(Normalization_normalized_frac));
  _6_Normalize_Output Normalization_2 (
    .Input_Significand(Rounding_output_significand), .Input_Exponent(Normalization_normalized_expo),
    .overflow(Overflow), .undeflow(underflow), .Normalized_frac(Output_Significand),
    .Normalized_expo(Output_exponent));  // open: _29__Position, Position, present
  _10_32Bit_MUX u_10_32bit_mux_1 (
    .G(1'b0), .S(n7408_1_p3), .A({Output_sign, Output_exponent, Output_Significand[28:10]}), .B({32{1'b0}}),
    .GND(1'b0), .Y(Output_result));  // open: Vcc

  // Notes on the sheet:
  //   sign
  //   sign
  //   fraction 19 bits
  //   exp 12 bits
  //   fraction 19 bits
  //   exp 12 bits
endmodule

module _2_Alignment_Input (
  input  [18:0] Fraction_Bit_A,
  input  [18:0] Fraction_Bit_B,
  input  [11:0] Exp_Bit_A,
  input  [11:0] Exp_Bit_B,
  input  Sign_Bit_A,
  input  Sign_Bit_B,
  output [21:0] Fraction_Bit_A_2,
  output [21:0] Fraction_Shifted,
  output [11:0] Exp_difference,
  output out_10,
  output [11:0] Larger_Exp,
  output Output_sign,
  output Equal_exponent
);

  wire comparator_1_gt, comparator_1_lt, n7404_1_p2, n74157_1_p4, n74157_1_p7;
  wire [11:0] n9_12bit_mux_1_output;
  wire [21:0] n8_22bit_mux_1_out_6;

  _8_22Bit_MUX u_8_22bit_mux_1 (
    .S(comparator_1_gt), .G(1'b0), .VCC(1'b1), .in_4({3'b001, Fraction_Bit_A}),
    .in_5({3'b001, Fraction_Bit_B}), .out_6(n8_22bit_mux_1_out_6));
  _9_12Bit_MUX u_9_12bit_mux_1 (.S(comparator_1_gt), .A(Exp_Bit_A), .B(Exp_Bit_B), .Output(n9_12bit_mux_1_output));
  _9_12Bit_MUX u_9_12bit_mux_2 (.S(comparator_1_lt), .A(Exp_Bit_A), .B(Exp_Bit_B), .Output(Larger_Exp));
  _8_22Bit_MUX u_8_22bit_mux_2 (
    .S(n7404_1_p2), .G(1'b0), .VCC(1'b1), .in_4({3'b001, Fraction_Bit_A}), .in_5({3'b001, Fraction_Bit_B}),
    .out_6(Fraction_Bit_A_2));
  Comparator #(.width(12), .mode("unsigned")) comparator_1 (
    .a(Exp_Bit_A), .b(Exp_Bit_B), .gt(comparator_1_gt), .eq(Equal_exponent), .lt(comparator_1_lt));
  // _74157 74157_1: pin names not known; wires that end beside it: comparator_1_gt, Sign_Bit_A, Sign_Bit_B, n74157_1_p4, Sign_Bit_B, Sign_Bit_A, n74157_1_p7, 1'b0, 1'b1, 1'b0
  // _7404 7404_1: pin names not known; wires that end beside it: comparator_1_gt, n7404_1_p2
  Subtractor_part #(.width(12)) subtractor_1 (
    .a(Larger_Exp), .b(n9_12bit_mux_1_output), .out(Exp_difference), .bin(1'b0), .bout(out_10));
  _3_Number_Shifter u_3_number_shifter_1 (
    .significand(n8_22bit_mux_1_out_6), .Exp_difference(Exp_difference), .Fraction_Shifted(Fraction_Shifted));
  _4_Sign_Bit_Detection u_4_sign_bit_detection_1 (
    .sign_Bit_A(n74157_1_p4), .sign_bit_B(n74157_1_p7), .Significand_A(Fraction_Shifted),
    .Significand_B(Fraction_Bit_A_2), .output_sign(Output_sign));

  // Notes on the sheet:
  //   22 bit mux
  //   22 bit mux
  //   12 Bit mux
  //   12 bit Comparator
  //   12 bit mux
  //   if A>B
  //   if A<B
  //   12 bit subtractor
  //   sign bit decider
  //   shifter
endmodule

module _3_Number_Shifter (
  input  [21:0] significand,
  input  [11:0] Exp_difference,
  output [21:0] Fraction_Shifted
);

  wire comparator_1_gt;
  wire [4:0] bit_extender_1_out;
  wire [21:0] shifter_1_out;

  Bit_Extender #(.in_width(12), .out_width(5)) bit_extender_1 (.in(Exp_difference), .out(bit_extender_1_out));
  Shifter #(.width(22), .shift("lr")) shifter_1 (.in(significand), .\dist (bit_extender_1_out), .out(shifter_1_out));
  Comparator #(.width(12), .mode("unsigned")) comparator_1 (
    .a(Exp_difference), .b(12'h1f), .gt(comparator_1_gt));  // open: eq, lt
  _8_22Bit_MUX u_8_22bit_mux_1 (
    .S(comparator_1_gt), .G(1'b0), .VCC(1'b1), .in_4(shifter_1_out), .in_5({22{1'b0}}),
    .out_6(Fraction_Shifted));

  // Notes on the sheet:
  //   (31)decimal 
  //   Shifter
  //   Comparator
  //   A
  //   22 bit mux
  //   B
endmodule

module _4_Sign_Bit_Detection (
  input  sign_Bit_A,
  input  sign_bit_B,
  input  [21:0] Significand_A,
  input  [21:0] Significand_B,
  output output_sign
);

  wire comparator_1_eq, comparator_1_gt, n7408_1_p3, n74157_1_p1, n74157_1_p4;

  Comparator #(.width(22), .mode("unsigned")) comparator_1 (
    .a(Significand_A), .b(Significand_B), .gt(comparator_1_gt), .eq(comparator_1_eq));  // open: lt
  // _74157 74157_1: pin names not known; wires that end beside it: n74157_1_p1, sign_Bit_A, sign_bit_B, n74157_1_p4, 1'b0
  // _7404 7404_1: pin names not known; wires that end beside it: comparator_1_gt, n74157_1_p1
  // _7408 7408_1: pin names not known; wires that end beside it: sign_Bit_A, sign_bit_B, n7408_1_p3
  // _74157 74157_2: pin names not known; wires that end beside it: comparator_1_eq, n74157_1_p4, n7408_1_p3, output_sign, 1'b0

  // Notes on the sheet:
  //   comparator
  //   larger's sign
endmodule

module _5_Adder_Circuit (
  input  sign_bit_A,
  input  sign_bit_B,
  input  [21:0] Significand_A,
  input  [21:0] Significand_B,
  output [31:0] Output_significand,
  output out_6,
  output out_7
);

  wire comparator_1_gt, n7404_1_p2, n7486_1_p3;
  wire [31:0] adder_1_out, n10_32bit_mux_1_y, n10_32bit_mux_2_y, subtractor_1_out;

  // _7486 7486_1: pin names not known; wires that end beside it: sign_bit_A, sign_bit_B, n7486_1_p3, 1'b0, 1'b1
  Adder #(.width(32)) adder_1 (
    .a({Significand_A, {10{1'b0}}}), .b({Significand_B, {10{1'b0}}}), .out(adder_1_out), .cin(1'b0),
    .cout(out_6));
  _10_32Bit_MUX u_10_32bit_mux_1 (
    .G(1'b0), .S(comparator_1_gt), .A({Significand_A, {10{1'b0}}}), .B({Significand_B, {10{1'b0}}}),
    .GND(1'b0), .Vcc(1'b1), .Y(n10_32bit_mux_1_y));
  Comparator #(.width(32), .mode("unsigned")) comparator_1 (
    .a({Significand_A, {10{1'b0}}}), .b({Significand_B, {10{1'b0}}}), .gt(comparator_1_gt));  // open: eq, lt
  _10_32Bit_MUX u_10_32bit_mux_2 (
    .G(1'b0), .S(n7404_1_p2), .A({Significand_A, {10{1'b0}}}), .B({Significand_B, {10{1'b0}}}), .GND(1'b0),
    .Vcc(1'b1), .Y(n10_32bit_mux_2_y));
  // _7404 7404_1: pin names not known; wires that end beside it: comparator_1_gt, n7404_1_p2
  _10_32Bit_MUX u_10_32bit_mux_3 (
    .G(1'b0), .S(n7486_1_p3), .A(adder_1_out), .B(subtractor_1_out), .GND(1'b0), .Vcc(1'b1),
    .Y(Output_significand));
  Subtractor_part #(.width(32)) subtractor_1 (
    .a(n10_32bit_mux_2_y), .b(n10_32bit_mux_1_y), .out(subtractor_1_out), .bin(1'b0), .bout(out_7));

  // Notes on the sheet:
  //   32 bit mux
  //   comparator
  //   32bit mux
  //   32 bit mux
endmodule

module _6_Normalize_Output (
  input  [31:0] Input_Significand,
  input  [11:0] Input_Exponent,
  output [4:0] _29__Position,
  output [4:0] Position,
  output [31:0] Normalized_frac,
  output present,
  output [11:0] Normalized_expo,
  output undeflow,
  output overflow
);

  wire comparator_1_eq, comparator_1_lt, comparator_2_eq, comparator_2_lt;
  wire [11:0] _12Bit_MUX_2_output, adder_1_out, bit_extender_1_out, subtractor_2_out;
  wire [31:0] _32Bit_MUX_2_y, shifter_1_out, shifter_2_out;

  BitFinder #(.width(32), .\type ("high1")) bitfinder_1 (.in(Input_Significand), .index(Position), .found(present));
  Subtractor_part #(.width(5)) subtractor_1 (.a(5'b11101), .b(Position), .out(_29__Position));  // open: bin, bout
  Comparator #(.width(5), .mode("unsigned")) comparator_1 (
    .a(Position), .b(5'b11101), .eq(comparator_1_eq), .lt(comparator_1_lt));  // open: gt
  Shifter #(.width(32), .shift("lr")) shifter_1 (.in(Input_Significand), .\dist (5'b00001), .out(shifter_1_out));
  _9_12Bit_MUX _12Bit_MUX (.S(comparator_1_eq), .A(_12Bit_MUX_2_output), .B(Input_Exponent), .Output(Normalized_expo));
  _10_32Bit_MUX _32Bit_MUX (
    .G(1'b0), .S(comparator_1_eq), .A(_32Bit_MUX_2_y), .B(Input_Significand), .Vcc(1'b1), .Y(Normalized_frac));  // open: GND
  Shifter #(.width(32)) shifter_2 (.in(Input_Significand), .\dist (_29__Position), .out(shifter_2_out));
  assign bit_extender_1_out = {{7{1'b0}}, _29__Position};  // Bit_Extender bit_extender_1
  _10_32Bit_MUX _32Bit_MUX_2 (
    .G(1'b0), .S(comparator_1_lt), .A(shifter_1_out), .B(shifter_2_out), .Vcc(1'b1), .Y(_32Bit_MUX_2_y));  // open: GND
  Adder #(.width(12)) adder_1 (.a(Input_Exponent), .b(12'h1), .out(adder_1_out), .cin(1'b0));  // open: cout
  Subtractor_part #(.width(12)) subtractor_2 (
    .a(Input_Exponent), .b(bit_extender_1_out), .out(subtractor_2_out), .bin(1'b0));  // open: bout
  _9_12Bit_MUX _12Bit_MUX_2 (.S(comparator_1_lt), .A(adder_1_out), .B(subtractor_2_out), .Output(_12Bit_MUX_2_output));
  Comparator #(.width(12), .mode("unsigned")) comparator_2 (
    .a(Normalized_expo), .b({12{1'b0}}), .eq(comparator_2_eq), .lt(comparator_2_lt));  // open: gt
  Comparator #(.width(12), .mode("unsigned")) comparator_3 (
    .a(Normalized_expo), .b(12'hffe), .gt(overflow));  // open: eq, lt
  // _7432 7432_1: pin names not known; wires that end beside it: comparator_2_eq, comparator_2_lt, undeflow
endmodule

module _7_Rounding_Bits (
  input  [31:0] Input_significand,
  output [31:0] Output_Significand
);

  wire n7432_1_p3, n7432_1_p6, n7432_1_p9, n7432_1_p12, n7432_2_p1, n7432_2_p2, n7432_2_p3, n7432_2_p5,
       n7432_2_p9;
  wire [8:8] n7432_2_p6;

  // _7432 7432_1: pin names not known; wires that end beside it: Input_significand[5], Input_significand[4], n7432_1_p3, n7432_1_p3, Input_significand[3], n7432_1_p6, Input_significand[2], n7432_1_p6, n7432_1_p9, n7432_1_p9, Input_significand[1], n7432_1_p12
  // _7432 7432_2: pin names not known; wires that end beside it: n7432_2_p1, n7432_2_p2, n7432_2_p3, n7432_2_p3, n7432_2_p5, n7432_2_p6[8], n7432_1_p12, Input_significand[0], n7432_2_p9
  // _7408 7408_1: pin names not known; wires that end beside it: Input_significand[7], Input_significand[6], n7432_2_p2, Input_significand[7], n7432_2_p9, n7432_2_p1, Input_significand[7], Input_significand[8], n7432_2_p5
  Adder #(.width(32)) adder_1 (
    .a(Input_significand), .b({{23{1'b0}}, n7432_2_p6[8], {8{1'b0}}}), .out(Output_Significand), .cin(1'b0));  // open: cout

  // Notes on the sheet:
  //   P
  //   G
  //   R
  //   S
  //   GR
  //   GS
  //   GR+GS+GP
  //   GP
endmodule

module _0_Block_Diagram (
  input  [31:0] Number_A,
  input  [31:0] Number_B,
  output [31:0] Output,
  output Overflow,
  output Underflow
);

  _1_Main_Circuit Floating_Point (
    .Number_A(Number_A), .Number_B(Number_B), .Overflow(Overflow), .underflow(Underflow),
    .Output_result(Output));  // open: Output_Significand, Output_exponent, Output_sign, equal_expononet
endmodule

module OR_12Bit (
  input  in_1,
  input  in_2,
  input  in_3,
  input  in_4,
  input  in_5,
  input  in_6,
  input  in_7,
  input  in_8,
  input  in_9,
  input  in_10,
  input  in_11,
  input  in_12,
  output \output 
);

  wire n7432_1_p3, n7432_1_p6, n7432_1_p11, n7432_1_p14, n7432_2_p3, n7432_2_p6, n7432_2_p10, n7432_2_p13,
       n7432_3_p3, n7432_3_p6;

  // _7432 7432_1: pin names not known; wires that end beside it: in_1, in_2, n7432_1_p3, n7432_1_p3, in_3, n7432_1_p6, 1'b0, 1'b1, n7432_1_p6, in_4, n7432_1_p11, n7432_1_p11, in_5, n7432_1_p14
  // _7432 7432_2: pin names not known; wires that end beside it: n7432_1_p14, in_6, n7432_2_p3, n7432_2_p3, in_7, n7432_2_p6, 1'b0, n7432_2_p6, in_8, n7432_2_p10, n7432_2_p10, in_9, n7432_2_p13
  // _7432 7432_3: pin names not known; wires that end beside it: n7432_2_p13, in_10, n7432_3_p3, n7432_3_p3, in_11, n7432_3_p6, 1'b0, in_12, n7432_3_p6, \output 
endmodule

module AND_12Bit (
  input  in_1,
  input  in_2,
  input  in_3,
  input  in_4,
  input  in_5,
  input  in_6,
  input  in_7,
  input  in_8,
  input  in_9,
  input  in_10,
  input  in_11,
  input  in_12,
  output \output 
);

  wire n7408_1_p3, n7408_1_p6, n7408_1_p11, n7408_1_p14, n7408_2_p3, n7408_2_p6, n7408_2_p10, n7408_2_p13,
       n7408_3_p3, n7408_3_p6;

  // _7408 7408_1: pin names not known; wires that end beside it: in_1, in_2, n7408_1_p3, n7408_1_p3, in_3, n7408_1_p6, 1'b0, 1'b1, n7408_1_p6, in_4, n7408_1_p11, n7408_1_p11, in_5, n7408_1_p14
  // _7408 7408_2: pin names not known; wires that end beside it: n7408_1_p14, in_6, n7408_2_p3, n7408_2_p3, in_7, n7408_2_p6, 1'b0, n7408_2_p6, in_8, n7408_2_p10, n7408_2_p10, in_9, n7408_2_p13
  // _7408 7408_3: pin names not known; wires that end beside it: n7408_2_p13, in_10, n7408_3_p3, n7408_3_p3, in_11, n7408_3_p6, 1'b0, in_12, n7408_3_p6, \output 
endmodule

module Overflow_Underflow (
  input  _11th_bit__From_exp_subt,
  input  At_least_one_1,
  input  [11:0] Normalized_exp,
  input  [11:0] Rounded_Exp,
  output Underflow,
  output Overflow
);

  wire AND_12Bit_2_output, AND_12Bit_output, n7404_1_p2, n7408_1_p3, OR_12Bit_output;

  OR_12Bit OR_12Bit (
    .in_1(Normalized_exp[0]), .in_2(Normalized_exp[1]), .in_3(Normalized_exp[2]), .in_4(Normalized_exp[3]),
    .in_5(Normalized_exp[4]), .in_6(Normalized_exp[5]), .in_7(Normalized_exp[6]), .in_8(Normalized_exp[7]),
    .in_9(Normalized_exp[8]), .in_10(Normalized_exp[9]), .in_11(Normalized_exp[10]),
    .in_12(Normalized_exp[11]), .\output (OR_12Bit_output));
  AND_12Bit AND_12Bit (
    .in_1(Normalized_exp[0]), .in_2(Normalized_exp[1]), .in_3(Normalized_exp[2]), .in_4(Normalized_exp[3]),
    .in_5(Normalized_exp[4]), .in_6(Normalized_exp[5]), .in_7(Normalized_exp[6]), .in_8(Normalized_exp[7]),
    .in_9(Normalized_exp[8]), .in_10(Normalized_exp[9]), .in_11(Normalized_exp[10]),
    .in_12(Normalized_exp[11]), .\output (AND_12Bit_output));
  AND_12Bit AND_12Bit_2 (
    .in_1(Rounded_Exp[0]), .in_2(Rounded_Exp[1]), .in_3(Rounded_Exp[2]), .in_4(Rounded_Exp[3]),
    .in_5(Rounded_Exp[4]), .in_6(Rounded_Exp[5]), .in_7(Rounded_Exp[6]), .in_8(Rounded_Exp[7]),
    .in_9(Rounded_Exp[8]), .in_10(Rounded_Exp[9]), .in_11(Rounded_Exp[10]), .in_12(Rounded_Exp[11]),
    .\output (AND_12Bit_2_output));
  // _7404 7404_1: pin names not known; wires that end beside it: OR_12Bit_output, n7404_1_p2, 1'b0, 1'b1
  // _7408 7408_1: pin names not known; wires that end beside it: At_least_one_1, n7404_1_p2, n7408_1_p3, 1'b0, 1'b1
  // _7432 7432_1: pin names not known; wires that end beside it: _11th_bit__From_exp_subt, n7408_1_p3, Underflow, AND_12Bit_output, AND_12Bit_2_output, Overflow, 1'b0, 1'b1
endmodule

module Compare_Exponent (
  input  [11:0] Exponent_A,
  input  [11:0] Exponent_B,
  output [11:0] Exponent_Difference,
  output Exp_A___Exp_B,
  output [11:0] Larger_Exp
);

  wire [11:0] negator_1_out, subtractor_1_out;

  Subtractor_part #(.width(12)) subtractor_1 (
    .a(Exponent_B), .b(Exponent_A), .out(subtractor_1_out), .bin(1'b0), .bout(Exp_A___Exp_B));
  Negator #(.width(12)) negator_1 (.in(subtractor_1_out), .out(negator_1_out));
  Multiplexer #(.width(12), .disabled(0), .enable("false")) multiplexer_1 (
    .in0(Exponent_B), .in1(Exponent_A), .out(Larger_Exp), .sel(Exp_A___Exp_B));
  Multiplexer #(.width(12), .disabled(0), .enable("false")) multiplexer_2 (
    .in0(subtractor_1_out), .in1(negator_1_out), .out(Exponent_Difference), .sel(Exp_A___Exp_B));
endmodule

module Sign_Bit_2_s_Complement (
  input  sign,
  input  [31:0] frac_in,
  output [31:0] frac_out
);

  wire [31:0] negator_1_out;

  Negator #(.width(32)) negator_1 (.in(frac_in), .out(negator_1_out));
  MUX_32Bit mux_32bit_1 (.in_1(sign), .Input_0(negator_1_out), .Input_1(frac_in), .Output(frac_out));
endmodule

module MUX_32Bit (
  input  in_1,
  input  [31:0] Input_0,
  input  [31:0] Input_1,
  output [31:0] Output
);

  // _74157 74157_1: pin names not known; wires that end beside it: in_1, Input_0[0], Input_1[0], Output[0], Input_0[1], Input_1[1], Output[1], 1'b0, 1'b1, 1'b0, Input_0[2], Input_1[2], Output[2], Input_0[3], Input_1[3], Output[3]
  // _74157 74157_2: pin names not known; wires that end beside it: in_1, Input_0[4], Input_1[4], Output[4], Input_0[5], Input_1[5], Output[5], 1'b0, 1'b1, 1'b0, Input_0[6], Input_1[6], Output[6], Input_0[7], Input_1[7], Output[7]
  // _74157 74157_3: pin names not known; wires that end beside it: in_1, Input_0[8], Input_1[8], Output[8], Input_0[9], Input_1[9], Output[9], 1'b0, 1'b1, 1'b0, Input_0[10], Input_1[10], Output[10], Input_0[11], Input_1[11], Output[11]
  // _74157 74157_4: pin names not known; wires that end beside it: in_1, Input_0[12], Input_1[12], Output[12], Input_0[13], Input_1[13], Output[13], 1'b0, 1'b1, 1'b0, Input_0[14], Input_1[14], Output[14], Input_0[15], Input_1[15], Output[15]
  // _74157 74157_5: pin names not known; wires that end beside it: in_1, Input_0[16], Input_1[16], Output[16], Input_0[17], Input_1[17], Output[17], 1'b0, 1'b1, 1'b0, Input_0[18], Input_1[18], Output[18], Input_0[19], Input_1[19], Output[19]
  // _74157 74157_6: pin names not known; wires that end beside it: in_1, Input_0[20], Input_1[20], Output[20], Input_0[21], Input_1[21], Output[21], 1'b0, 1'b1, 1'b0, Input_0[22], Input_1[22], Output[22], Input_0[23], Input_1[23], Output[23]
  // _74157 74157_7: pin names not known; wires that end beside it: in_1, Input_0[24], Input_1[24], Output[24], Input_0[25], Input_1[25], Output[25], 1'b0, 1'b1, 1'b0, Input_0[26], Input_1[26], Output[26], Input_0[27], Input_1[27], Output[27]
  // _74157 74157_8: pin names not known; wires that end beside it: in_1, Input_0[28], Input_1[28], Output[28], Input_0[29], Input_1[29], Output[29], 1'b0, 1'b1, 1'b0, Input_0[31], Input_1[31], Output[31], Input_0[30], Input_1[30], Output[30]
endmodule

module Padding (
  input  [18:0] Fraction,
  input  [11:0] Exponent,
  output [31:0] out_3
);

  OR_12Bit or_12bit_1 (
    .in_1(Exponent[0]), .in_2(Exponent[1]), .in_3(Exponent[2]), .in_4(Exponent[3]), .in_5(Exponent[4]),
    .in_6(Exponent[5]), .in_7(Exponent[6]), .in_8(Exponent[7]), .in_9(Exponent[8]), .in_10(Exponent[9]),
    .in_11(Exponent[10]), .in_12(Exponent[11]), .\output (out_3[29]));

  assign {out_3[31:30], out_3[28:0]} = {2'b00, Fraction, {10{1'b0}}};
endmodule

module Adder2 (
  input  [31:0] Large_Significand,
  input  sign_L,
  input  sign_S,
  input  [31:0] Small_significand,
  output [31:0] out_5
);

  wire [31:0] sign_bit_2_s_complement_1_frac_out, sign_bit_2_s_complement_2_frac_out;

  Sign_Bit_2_s_Complement sign_bit_2_s_complement_1 (
    .sign(sign_L), .frac_in(Large_Significand), .frac_out(sign_bit_2_s_complement_1_frac_out));
  Sign_Bit_2_s_Complement sign_bit_2_s_complement_2 (
    .sign(sign_S), .frac_in(Small_significand), .frac_out(sign_bit_2_s_complement_2_frac_out));
  Adder #(.width(32)) adder_1 (
    .a(sign_bit_2_s_complement_1_frac_out), .b(sign_bit_2_s_complement_2_frac_out), .out(out_5), .cin(1'b0));  // open: cout
endmodule

module Subtractor (
  input  [11:0] A,
  input  [11:0] B,
  output [11:0] A_B,
  output MSB__isNeg
);

  wire subtractor_1_bout;

  Subtractor_part #(.width(12)) subtractor_1 (.a(A), .b(B), .out(A_B), .bout(subtractor_1_bout));  // open: bin
  Subtractor_part #(.width(1)) subtractor_2 (
    .a(1'b0), .b(B[11]), .out(MSB__isNeg), .bin(subtractor_1_bout));  // open: bout
endmodule

module Align2 (
  input  [31:0] Small_Significand_IN,
  input  [11:0] expdiff,
  output [31:0] Small_Significand_OUT
);

  wire or_7bit_1_output;
  wire [31:0] shifter_1_out;

  OR_7Bit or_7bit_1 (
    .in_1(expdiff[5]), .in_2(expdiff[6]), .in_3(expdiff[7]), .in_4(expdiff[8]), .in_5(expdiff[9]),
    .in_6(expdiff[10]), .in_7(expdiff[11]), .\output (or_7bit_1_output));
  Shifter #(.width(32), .shift("lr")) shifter_1 (.in(Small_Significand_IN), .\dist (expdiff[4:0]), .out(shifter_1_out));
  MUX_32Bit mux_32bit_1 (
    .in_1(or_7bit_1_output), .Input_0(shifter_1_out), .Input_1({32{1'b0}}), .Output(Small_Significand_OUT));
endmodule

module OR_7Bit (
  input  in_1,
  input  in_2,
  input  in_3,
  input  in_4,
  input  in_5,
  input  in_6,
  input  in_7,
  output \output 
);

  wire n7432_1_p3, n7432_1_p6, n7432_1_p11, n7432_1_p14, n7432_2_p3;

  // _7432 7432_1: pin names not known; wires that end beside it: in_1, in_2, n7432_1_p3, n7432_1_p3, in_3, n7432_1_p6, 1'b0, 1'b1, n7432_1_p6, in_4, n7432_1_p11, n7432_1_p11, in_5, n7432_1_p14
  // _7432 7432_2: pin names not known; wires that end beside it: n7432_1_p14, in_6, n7432_2_p3, n7432_2_p3, in_7, \output 
endmodule

module _8_22Bit_MUX (
  input  S,
  input  G,
  input  VCC,
  input  [21:0] in_4,
  input  [21:0] in_5,
  output [21:0] out_6
);

  // _74157 74157_1: pin names not known; wires that end beside it: in_5[12], S, in_4[12], in_5[12], out_6[12], in_4[13], in_5[13], out_6[13], VCC, G, in_4[14], in_5[14], out_6[14], in_4[15], in_5[15], out_6[15]
  // _74157 74157_2: pin names not known; wires that end beside it: S, in_4[0], in_5[0], out_6[0], in_4[1], in_5[1], out_6[1], VCC, G, in_4[2], in_5[2], out_6[2], in_4[3], in_5[3], out_6[3]
  // _74157 74157_3: pin names not known; wires that end beside it: S, in_4[4], in_5[4], out_6[4], in_4[5], in_5[5], out_6[5], VCC, G, in_4[6], in_5[6], out_6[6], in_4[7], in_5[7], out_6[7]
  // _74157 74157_4: pin names not known; wires that end beside it: S, in_4[16], in_5[16], out_6[16], in_4[17], in_5[17], out_6[17], VCC, G, in_4[18], in_5[18], out_6[18], in_4[19], in_5[19], out_6[19], out_6[19], out_6[20]
  // _74157 74157_5: pin names not known; wires that end beside it: S, in_4[8], in_5[8], out_6[8], in_4[9], in_5[9], out_6[9], VCC, G, in_4[10], in_5[10], out_6[10], in_4[11], in_5[11], out_6[11]
  // _74157 74157_6: pin names not known; wires that end beside it: S, in_4[20], in_5[20], out_6[20], in_4[21], in_5[21], out_6[21], VCC, G, out_6[14]
endmodule

module _9_12Bit_MUX (
  input  S,
  input  [11:0] A,
  input  [11:0] B,
  output [11:0] Output
);

  // _74157 74157_1: pin names not known; wires that end beside it: S, A[8], B[8], Output[8], A[11], B[11], Output[11], 1'b1, 1'b0, A[9], B[9], Output[9], A[10], B[10], Output[10]
  // _74157 74157_2: pin names not known; wires that end beside it: S, A[0], B[0], Output[0], A[1], B[1], Output[1], 1'b1, 1'b0, A[2], B[2], Output[2], A[3], B[3], Output[3]
  // _74157 74157_3: pin names not known; wires that end beside it: S, A[4], B[4], Output[4], A[5], B[5], Output[5], 1'b1, 1'b0, A[6], B[6], Output[6], A[7], B[7], Output[7]
endmodule

module _10_32Bit_MUX (
  input  G,
  input  Vcc,
  input  S,
  input  [31:0] A,
  input  [31:0] B,
  input  GND,
  output [31:0] Y
);

  // _74157 74157_1: pin names not known; wires that end beside it: S, A[0], B[0], Y[0], A[1], B[1], Y[1], GND, Vcc, G, A[3], B[3], Y[3], A[2], B[2], Y[2]
  // _74157 74157_2: pin names not known; wires that end beside it: S, A[20], B[20], Y[20], A[21], B[21], Y[21], GND, Vcc, G, A[23], B[23], Y[23], A[22], B[22], Y[22]
  // _74157 74157_3: pin names not known; wires that end beside it: S, A[4], B[4], Y[4], A[5], B[5], Y[5], GND, G, G, A[7], B[7], Y[7], A[6], B[6], Y[6]
  // _74157 74157_4: pin names not known; wires that end beside it: S, A[8], B[8], Y[8], A[9], B[9], Y[9], GND, Vcc, G, A[11], B[11], Y[11], A[10], B[10], Y[10]
  // _74157 74157_5: pin names not known; wires that end beside it: S, A[24], B[24], Y[24], A[25], B[25], Y[25], GND, Vcc, G, A[27], B[27], Y[27], A[26], B[26], Y[26]
  // _74157 74157_6: pin names not known; wires that end beside it: S, A[12], B[12], Y[12], A[13], B[13], Y[13], GND, Vcc, G, A[15], B[15], Y[15], A[14], B[14], Y[14]
  // _74157 74157_7: pin names not known; wires that end beside it: S, A[28], B[28], Y[28], A[29], B[29], Y[29], GND, Vcc, G, A[31], B[31], Y[31], A[30], B[30], Y[30]
  // _74157 74157_8: pin names not known; wires that end beside it: S, A[16], B[16], Y[16], A[17], B[17], Y[17], GND, Vcc, G, A[19], B[19], Y[19], A[18], B[18], Y[18]
endmodule

// Output
module _11_Block_Diagram_2 (
  input  [18:0] Input_A_Fraction,
  input  [11:0] Input_A_Exponent,
  input  in_3,
  input  Input_A_Sign,
  input  [31:0] Input_A,
  input  [18:0] Input_B_Fraction,
  input  [11:0] Input_B_Exponent,
  input  in_8,
  input  Input_B_Sign,
  input  [31:0] Input_B,
  output [31:0] out_11,
  output [31:0] Output,
  output [18:0] Output_Fraction,
  output Underflow,
  output [11:0] Output_Exponent,
  output Overflow,
  output Output_Sign,
  output [31:0] out_18
);

  Multiplexer #(.width(32), .disabled(0), .enable("false")) multiplexer_1 (
    .in0({Input_A_Sign, Input_A_Exponent, Input_A_Fraction}), .in1(Input_A), .out(out_11), .sel(in_3));
  Multiplexer #(.width(32), .disabled(0), .enable("false")) multiplexer_2 (
    .in0({Input_B_Sign, Input_B_Exponent, Input_B_Fraction}), .in1(Input_B), .out(out_18), .sel(in_8));
  _1_Main_Circuit Floating_Point (
    .Number_A(out_11), .Number_B(out_18), .Overflow(Overflow), .underflow(Underflow), .Output_result(Output));  // open: Output_Significand, Output_exponent, Output_sign, equal_expononet

  assign Output_Exponent = Output[30:19];
  assign Output_Fraction = Output[18:0];
  assign Output_Sign = Output[31];

  // Notes on the sheet:
  //   MUX selection
  //   Select 0 for split input
  //   Select 1 for full input
endmodule
